// Logisim project KATHANbus.circ as structural Verilog: 2 circuits, main circuit main
module main (
  input  [1:0] in_1,
  input  [3:0] in_2,
  input  [3:0] in_3,
  input  [3:0] in_4,
  input  [3:0] in_5,
  input  in_6,
  output [3:0] out_7
);

  wire clock_1_out;
  wire [3:0] register_1_q, register_2_q, register_3_q, register_4_q;

  Register #(.width(4)) register_1 (.D(in_2), .en(1'b1), .Q(register_1_q), .clk(clock_1_out), .clr(in_6));
  Clock clock_1 (.out(clock_1_out));
  Multiplexer #(.select(2), .enable("false")) multiplexer_1 (
    .in0(register_4_q[3]), .in1(register_3_q[3]), .in2(register_2_q[3]), .in3(register_1_q[3]),
    .out(out_7[3]), .sel(in_1));
  Multiplexer #(.select(2), .enable("false")) multiplexer_2 (
    .in0(register_4_q[2]), .in1(register_3_q[2]), .in2(register_2_q[2]), .in3(register_1_q[2]),
    .out(out_7[2]), .sel(in_1));
  Register #(.width(4)) register_2 (.D(in_3), .en(1'b1), .Q(register_2_q), .clk(clock_1_out), .clr(in_6));
  Register #(.width(4)) register_3 (.D(in_4), .en(1'b1), .Q(register_3_q), .clk(clock_1_out), .clr(in_6));
  Multiplexer #(.select(2), .enable("false")) multiplexer_3 (
    .in0(register_4_q[1]), .in1(register_3_q[1]), .in2(register_2_q[1]), .in3(register_1_q[1]),
    .out(out_7[1]), .sel(in_1));
  Multiplexer #(.select(2), .enable("false")) multiplexer_4 (
    .in0(register_4_q[0]), .in1(register_3_q[0]), .in2(register_2_q[0]), .in3(register_1_q[0]),
    .out(out_7[0]), .sel(in_1));
  Register #(.width(4)) register_4 (.D(in_5), .en(1'b1), .Q(register_4_q), .clk(clock_1_out), .clr(in_6));
endmodule

module CIRCUIT2 (
  input  [1:0] Select,
  input  [3:0] Input_for_Register_D,
  input  [3:0] Input_for_Register_C,
  input  [3:0] Input_for_Register_B,
  input  [3:0] Input_for_Register_A,
  input  in_6,
  output [3:0] Common_Bus,
  output [3:0] out_8,
  output [3:0] out_9,
  output [3:0] out_10,
  output [3:0] out_11
);

  wire clock_1_out, decoder_1_out0, decoder_1_out1, decoder_1_out2, decoder_1_out3;

  Decoder #(.select(2), .enable("false")) decoder_1 (
    .out0(decoder_1_out0), .out1(decoder_1_out1), .out2(decoder_1_out2), .out3(decoder_1_out3), .sel(Select));
  Register #(.width(4)) Register_D (.D(Input_for_Register_D), .en(1'b1), .Q(out_8), .clk(clock_1_out), .clr(in_6));
  Clock clock_1 (.out(clock_1_out));
  assign Common_Bus[3] = decoder_1_out0 ? out_11[3] : 1'bz;  // Controlled_Buffer controlled_buffer_1
  assign Common_Bus[3] = decoder_1_out1 ? out_10[3] : 1'bz;  // Controlled_Buffer controlled_buffer_2
  assign Common_Bus[3] = decoder_1_out2 ? out_9[3] : 1'bz;  // Controlled_Buffer controlled_buffer_3
  assign Common_Bus[3] = decoder_1_out3 ? out_8[3] : 1'bz;  // Controlled_Buffer controlled_buffer_4
  assign Common_Bus[2] = decoder_1_out0 ? out_11[2] : 1'bz;  // Controlled_Buffer controlled_buffer_5
  assign Common_Bus[2] = decoder_1_out1 ? out_10[2] : 1'bz;  // Controlled_Buffer controlled_buffer_6
  assign Common_Bus[2] = decoder_1_out2 ? out_9[2] : 1'bz;  // Controlled_Buffer controlled_buffer_7
  assign Common_Bus[2] = decoder_1_out3 ? out_8[2] : 1'bz;  // Controlled_Buffer controlled_buffer_8
  Register #(.width(4)) Register_C (.D(Input_for_Register_C), .en(1'b1), .Q(out_9), .clk(clock_1_out), .clr(in_6));
  Register #(.width(4)) Register_B (.D(Input_for_Register_B), .en(1'b1), .Q(out_10), .clk(clock_1_out), .clr(in_6));
  assign Common_Bus[1] = decoder_1_out0 ? out_11[1] : 1'bz;  // Controlled_Buffer controlled_buffer_9
  assign Common_Bus[1] = decoder_1_out1 ? out_10[1] : 1'bz;  // Controlled_Buffer controlled_buffer_10
  assign Common_Bus[1] = decoder_1_out2 ? out_9[1] : 1'bz;  // Controlled_Buffer controlled_buffer_11
  assign Common_Bus[1] = decoder_1_out3 ? out_8[1] : 1'bz;  // Controlled_Buffer controlled_buffer_12
  assign Common_Bus[0] = decoder_1_out0 ? out_11[0] : 1'bz;  // Controlled_Buffer controlled_buffer_13
  assign Common_Bus[0] = decoder_1_out1 ? out_10[0] : 1'bz;  // Controlled_Buffer controlled_buffer_14
  assign Common_Bus[0] = decoder_1_out2 ? out_9[0] : 1'bz;  // Controlled_Buffer controlled_buffer_15
  assign Common_Bus[0] = decoder_1_out3 ? out_8[0] : 1'bz;  // Controlled_Buffer controlled_buffer_16
  Register #(.width(4)) Register_A (.D(Input_for_Register_A), .en(1'b1), .Q(out_11), .clk(clock_1_out), .clr(in_6));

  // Notes on the sheet:
  //   23CS046
  //   A3
  //   B3
  //   C3
  //   D3
  //   A2
  //   C2
  //   B2
  //   D2
  //   A1
  //   B1
  //   C1
  //   D1
  //   A0
  //   B0
  //   C0
  //   D0
endmodule
