// Logisim project TRISTATEbus.circ as structural Verilog: 1 circuit, main circuit main
module main (
  input  [3:0] in_1,
  input  [3:0] in_2,
  input  [3:0] in_3,
  input  [3:0] in_4,
  input  [1:0] in_5,
  output [3:0] out_6
);

  wire clock_1_out, decoder_1_out0, decoder_1_out1, decoder_1_out2, decoder_1_out3;
  wire [3:0] register_1_q, register_2_q, register_3_q, register_4_q;

  Clock clock_1 (.out(clock_1_out));
  Register #(.width(4)) register_1 (.D(in_1), .Q(register_1_q), .clk(clock_1_out));  // open: en, clr
  Register #(.width(4)) register_2 (.D(in_2), .Q(register_2_q), .clk(clock_1_out));  // open: en, clr
  Register #(.width(4)) register_3 (.D(in_3), .Q(register_3_q), .clk(clock_1_out));  // open: en, clr
  Register #(.width(4)) register_4 (.D(in_4), .Q(register_4_q), .clk(clock_1_out));  // open: en, clr
  assign out_6[0] = decoder_1_out0 ? register_1_q[0] : 1'bz;  // Controlled_Buffer controlled_buffer_1
  assign out_6[0] = decoder_1_out1 ? register_2_q[0] : 1'bz;  // Controlled_Buffer controlled_buffer_2
  assign out_6[0] = decoder_1_out2 ? register_3_q[0] : 1'bz;  // Controlled_Buffer controlled_buffer_3
  assign out_6[1] = decoder_1_out0 ? register_1_q[1] : 1'bz;  // Controlled_Buffer controlled_buffer_4
  assign out_6[1] = decoder_1_out1 ? register_2_q[1] : 1'bz;  // Controlled_Buffer controlled_buffer_5
  assign out_6[1] = decoder_1_out2 ? register_3_q[1] : 1'bz;  // Controlled_Buffer controlled_buffer_6
  assign out_6[2] = decoder_1_out0 ? register_1_q[2] : 1'bz;  // Controlled_Buffer controlled_buffer_7
  assign out_6[2] = decoder_1_out1 ? register_2_q[2] : 1'bz;  // Controlled_Buffer controlled_buffer_8
  assign out_6[2] = decoder_1_out2 ? register_3_q[2] : 1'bz;  // Controlled_Buffer controlled_buffer_9
  assign out_6[3] = decoder_1_out0 ? register_1_q[3] : 1'bz;  // Controlled_Buffer controlled_buffer_10
  assign out_6[3] = decoder_1_out1 ? register_2_q[3] : 1'bz;  // Controlled_Buffer controlled_buffer_11
  assign out_6[3] = decoder_1_out2 ? register_3_q[3] : 1'bz;  // Controlled_Buffer controlled_buffer_12
  assign out_6[0] = decoder_1_out3 ? register_4_q[0] : 1'bz;  // Controlled_Buffer controlled_buffer_13
  assign out_6[1] = decoder_1_out3 ? register_4_q[1] : 1'bz;  // Controlled_Buffer controlled_buffer_14
  assign out_6[2] = decoder_1_out3 ? register_4_q[2] : 1'bz;  // Controlled_Buffer controlled_buffer_15
  assign out_6[3] = decoder_1_out3 ? register_4_q[3] : 1'bz;  // Controlled_Buffer controlled_buffer_16
  Decoder #(.select(2)) decoder_1 (
    .out0(decoder_1_out0), .out1(decoder_1_out1), .out2(decoder_1_out2), .out3(decoder_1_out3), .sel(in_5));  // open: en
endmodule
