// Logisim project add and sub.circ as structural Verilog: 1 circuit, main circuit main
module main (
  input  [3:0] A,
  input  [3:0] B,
  input  As,
  input  Bs,
  input  in_5,
  input  in_6,
  input  [3:0] in_7,
  input  [3:0] in_8,
  output out_9,
  output [3:0] out_10,
  output out_11,
  output [3:0] out_12,
  output out_13,
  output out_14,
  output [3:0] out_15
);

  wire adder_1_cout, comparator_1_eq, comparator_1_gt, comparator_1_lt, not_2_out, not_5_out, or_1_out,
       or_2_out, xor_1_out;
  wire [3:0] adder_1_out, controlled_buffer_2_out, not_3_out, not_4_out;

  not not_1 (out_9, As);
  xor xor_1 (xor_1_out, As, Bs);
  not not_2 (not_2_out, or_1_out);
  or or_1 (or_1_out, in_5, xor_1_out);
  assign not_3_out = ~B;  // NOT_Gate not_3, 4 bits wide
  Adder #(.width(4)) adder_1 (.a(A), .b(not_3_out), .out(adder_1_out), .cin(in_6), .cout(adder_1_cout));
  assign not_4_out = ~out_10;  // NOT_Gate not_4, 4 bits wide
  not not_5 (not_5_out, adder_1_cout);
  assign out_10 = not_2_out ? adder_1_out : 4'bz;  // Controlled_Buffer controlled_buffer_1
  assign controlled_buffer_2_out = not_5_out ? not_4_out : 4'bz;  // Controlled_Buffer controlled_buffer_2
  not not_6 (out_11, adder_1_cout);
  Comparator #(.width(4)) comparator_1 (
    .a(out_10), .b(in_8), .gt(comparator_1_gt), .eq(comparator_1_eq), .lt(comparator_1_lt));
  Adder #(.width(4)) adder_2 (.a(controlled_buffer_2_out), .b(in_7), .out(out_12));  // open: cin, cout
  assign out_14 = adder_1_cout ? comparator_1_eq : 1'bz;  // Controlled_Buffer controlled_buffer_3
  or or_2 (or_2_out, comparator_1_gt, comparator_1_lt);
  assign out_13 = adder_1_cout ? or_2_out : 1'bz;  // Controlled_Buffer controlled_buffer_4

  assign out_15 = out_10;
endmodule
