// Logisim project addonly.circ as structural Verilog: 1 circuit, main circuit main
module main (
  input  [3:0] A,
  input  [3:0] B,
  input  As,
  input  Bs,
  input  in_5,
  input  in_6,
  output out_7,
  output out_8,
  output out_9,
  output [3:0] out_10
);

  wire and_1_out, not_1_out;
  wire [3:0] adder_1_out;

  and and_1 (and_1_out, out_7, in_5);
  Adder #(.width(4)) adder_1 (.a(A), .b(B), .out(adder_1_out), .cin(in_6));  // open: cout
  xor xor_1 (out_7, As, Bs);
  assign out_10 = not_1_out ? adder_1_out : 4'bz;  // Controlled_Buffer controlled_buffer_1
  not not_1 (not_1_out, and_1_out);

  assign out_8 = As;
  assign out_9 = Bs;
endmodule
