// Logisim project arithmetic.circ as structural Verilog: 1 circuit, main circuit main
module main (
  input  CIN,
  input  A0,
  input  B0,
  input  A1,
  input  B1,
  input  A2,
  input  B2,
  input  A3,
  input  B3,
  input  [1:0] S1,
  input  S0,
  output out_12,
  output out_13,
  output out_14,
  output out_15,
  output out_16
);

  wire adder_1_cout, adder_2_cout, adder_3_cout, multiplexer_1_out, multiplexer_2_out, multiplexer_3_out,
       multiplexer_4_out, not_1_out, not_2_out, not_3_out, not_4_out, not_5_out;

  not not_1 (not_1_out, S0);
  not not_2 (not_2_out, B0);
  not not_3 (not_3_out, B1);
  not not_4 (not_4_out, B2);
  not not_5 (not_5_out, B3);
  Multiplexer #(.select(2), .enable("false")) multiplexer_1 (
    .in0(B0), .in1(not_2_out), .in2(S0), .in3(not_1_out), .out(multiplexer_1_out), .sel(S1));
  Multiplexer #(.select(2), .enable("false")) multiplexer_2 (
    .in0(B1), .in1(not_3_out), .in2(S0), .in3(not_1_out), .out(multiplexer_2_out), .sel(S1));
  Multiplexer #(.select(2), .enable("false")) multiplexer_3 (
    .in0(B2), .in1(not_4_out), .in2(S0), .in3(not_1_out), .out(multiplexer_3_out), .sel(S1));
  Multiplexer #(.select(2), .enable("false")) multiplexer_4 (
    .in0(B3), .in1(not_5_out), .in2(S0), .in3(not_1_out), .out(multiplexer_4_out), .sel(S1));
  Adder #(.width(1)) adder_1 (.a(A0), .b(multiplexer_1_out), .out(out_12), .cin(CIN), .cout(adder_1_cout));
  Adder #(.width(1)) adder_2 (.a(A1), .b(multiplexer_2_out), .out(out_13), .cin(adder_1_cout), .cout(adder_2_cout));
  Adder #(.width(1)) adder_3 (.a(A2), .b(multiplexer_3_out), .out(out_14), .cin(adder_2_cout), .cout(adder_3_cout));
  Adder #(.width(1)) adder_4 (.a(A3), .b(multiplexer_4_out), .out(out_15), .cin(adder_3_cout), .cout(out_16));
endmodule
