// Logisim project final add and sub.circ as structural Verilog: 1 circuit, main circuit main
module main (
  input  [3:0] A,
  input  [3:0] B,
  input  As,
  input  Bs,
  input  As_2,
  input  Bs_2,
  input  in_7,
  input  in_8,
  input  in_9,
  input  in_10,
  input  [3:0] in_11,
  input  [3:0] in_12,
  output out_13,
  output out_14,
  output out_15,
  output out_16,
  output [3:0] out_17,
  output [3:0] out_18,
  output out_19,
  output [3:0] out_20,
  output out_21,
  output out_22,
  output [3:0] out_23
);

  wire adder_1_cout, and_1_out, comparator_1_eq, comparator_1_gt, comparator_1_lt, not_2_out, not_5_out,
       not_7_out, or_1_out, or_2_out, xor_1_out;
  wire [3:0] adder_1_out, adder_3_out, controlled_buffer_2_out, not_3_out, not_4_out;

  not not_1 (out_14, As);
  xor xor_1 (xor_1_out, As, Bs);
  not not_2 (not_2_out, or_1_out);
  or or_1 (or_1_out, in_7, xor_1_out);
  assign not_3_out = ~B;  // NOT_Gate not_3, 4 bits wide
  Adder #(.width(4)) adder_1 (.a(A), .b(not_3_out), .out(adder_1_out), .cin(in_9), .cout(adder_1_cout));
  assign not_4_out = ~out_17;  // NOT_Gate not_4, 4 bits wide
  not not_5 (not_5_out, adder_1_cout);
  assign out_17 = not_2_out ? adder_1_out : 4'bz;  // Controlled_Buffer controlled_buffer_1
  assign controlled_buffer_2_out = not_5_out ? not_4_out : 4'bz;  // Controlled_Buffer controlled_buffer_2
  not not_6 (out_19, adder_1_cout);
  Comparator #(.width(4)) comparator_1 (
    .a(out_17), .b(in_12), .gt(comparator_1_gt), .eq(comparator_1_eq), .lt(comparator_1_lt));
  Adder #(.width(4)) adder_2 (.a(controlled_buffer_2_out), .b(in_11), .out(out_20));  // open: cin, cout
  assign out_22 = adder_1_cout ? comparator_1_eq : 1'bz;  // Controlled_Buffer controlled_buffer_3
  or or_2 (or_2_out, comparator_1_gt, comparator_1_lt);
  assign out_21 = adder_1_cout ? or_2_out : 1'bz;  // Controlled_Buffer controlled_buffer_4
  and and_1 (and_1_out, out_13, in_8);
  Adder #(.width(4)) adder_3 (.a(A), .b(B), .out(adder_3_out), .cin(in_10));  // open: cout
  xor xor_2 (out_13, As_2, Bs_2);
  assign out_18 = not_7_out ? adder_3_out : 4'bz;  // Controlled_Buffer controlled_buffer_5
  not not_7 (not_7_out, and_1_out);

  assign out_15 = As_2;
  assign out_16 = Bs_2;
  assign out_23 = out_17;

  // Notes on the sheet:
  //   23CE043
endmodule
