// Logisim project logical.circ as structural Verilog: 1 circuit, main circuit main
module main (
  input  A0,
  input  B0,
  input  A1,
  input  B1,
  input  A2,
  input  B2,
  input  A3,
  input  [1:0] S1,
  output out_9
);

  wire and_1_out, not_1_out, or_1_out, xor_1_out;

  and and_1 (and_1_out, A0, B0);
  or or_1 (or_1_out, A1, B1);
  not not_1 (not_1_out, A3);
  xor xor_1 (xor_1_out, A2, B2);
  Multiplexer #(.select(2), .enable("false")) multiplexer_1 (
    .in0(and_1_out), .in1(or_1_out), .in2(xor_1_out), .in3(not_1_out), .out(out_9), .sel(S1));
endmodule
