// Logisim project segment.circ as structural Verilog: 2 circuits, main circuit main
module main (
  input  a,
  input  b,
  input  c,
  input  d,
  output a_2,
  output b_2,
  output c_2,
  output d_2,
  output e,
  output f,
  output g
);

  wire nand_1_out, nand_2_out, nand_3_out, nand_4_out, nand_5_out, nand_6_out, nand_7_out, nand_8_out,
       nand_9_out, nand_10_out, nand_11_out, nand_12_out, nand_13_out, nand_14_out, nand_15_out, nand_16_out,
       nand_17_out, nand_18_out, nand_19_out, nand_20_out, nand_21_out, nand_22_out, nand_23_out,
       nand_24_out, nand_25_out, nand_26_out, nand_27_out, nand_29_out, nand_30_out, nand_31_out,
       nand_32_out, nand_33_out, nand_34_out, nand_35_out, nand_36_out, nand_37_out, nand_38_out,
       nand_39_out, nand_40_out, nand_41_out, nand_42_out, nand_43_out;

  nand nand_1 (nand_1_out, b, b);
  nand nand_2 (nand_2_out, d, d);
  nand nand_3 (nand_3_out, c, c);
  nand nand_4 (nand_4_out, d, d);
  nand nand_5 (nand_5_out, d, d);
  nand nand_6 (nand_6_out, b, b);
  nand nand_7 (nand_7_out, b, b);
  nand nand_8 (nand_8_out, d, d);
  nand nand_9 (nand_9_out, b, b);
  nand nand_10 (nand_10_out, d, d);
  nand nand_11 (nand_11_out, c, c);
  nand nand_12 (nand_12_out, b, b);
  nand nand_13 (nand_13_out, d, d);
  nand nand_14 (nand_14_out, d, d);
  nand nand_15 (nand_15_out, c, c);
  nand nand_16 (nand_16_out, d, d);
  nand nand_17 (nand_17_out, c, c);
  nand nand_18 (nand_18_out, d, d);
  nand nand_19 (nand_19_out, b, b);
  nand nand_20 (nand_20_out, c, c);
  nand nand_21 (nand_21_out, d, d);
  nand nand_22 (nand_22_out, nand_1_out, nand_2_out);
  nand nand_23 (nand_23_out, c, c);
  nand nand_24 (nand_24_out, b, d);
  nand nand_25 (nand_25_out, a, a);
  nand nand_26 (nand_26_out, nand_3_out, nand_4_out);
  nand nand_27 (nand_27_out, c, d);
  nand nand_28 (c_2, c, nand_5_out, nand_6_out);
  nand nand_29 (nand_29_out, nand_7_out, nand_8_out);
  nand nand_30 (nand_30_out, nand_9_out, c);
  nand nand_31 (nand_31_out, c, nand_10_out);
  nand nand_32 (nand_32_out, b, nand_11_out, d);
  nand nand_33 (nand_33_out, a, a);
  nand nand_34 (nand_34_out, nand_12_out, nand_13_out);
  nand nand_35 (nand_35_out, c, nand_14_out);
  nand nand_36 (nand_36_out, nand_15_out, nand_16_out);
  nand nand_37 (nand_37_out, b, nand_17_out);
  nand nand_38 (nand_38_out, b, nand_18_out);
  nand nand_39 (nand_39_out, a, a);
  nand nand_40 (nand_40_out, nand_19_out, c);
  nand nand_41 (nand_41_out, b, nand_20_out);
  nand nand_42 (nand_42_out, b, nand_21_out);
  nand nand_43 (nand_43_out, a, a);
  nand nand_44 (a_2, nand_22_out, nand_23_out, nand_24_out, nand_25_out);
  nand nand_45 (b_2, b, nand_26_out, nand_27_out);
  nand nand_46 (d_2, nand_29_out, nand_30_out, nand_31_out, nand_32_out, nand_33_out);
  nand nand_47 (e, nand_34_out, nand_35_out);
  nand nand_48 (f, nand_36_out, nand_37_out, nand_38_out, nand_39_out);
  nand nand_49 (g, nand_40_out, nand_41_out, nand_42_out, nand_43_out);
endmodule

module BCD (
  input  [5:0] in_1,
  input  in_2,
  input  in_3,
  input  in_4,
  input  in_5,
  input  in_6,
  input  in_7,
  input  in_8,
  input  in_9
);

  wire main_1_a_2, main_1_b_2, main_1_c_2, main_1_d_2, main_1_e, main_1_f, main_1_g, main_2_a_2, main_2_b_2,
       main_2_c_2, main_2_d_2, main_2_e, main_2_f, main_2_g;

  main main_1 (
    .a(in_6), .b(in_7), .c(in_8), .d(in_9), .a_2(main_1_a_2), .b_2(main_1_b_2), .c_2(main_1_c_2),
    .d_2(main_1_d_2), .e(main_1_e), .f(main_1_f), .g(main_1_g));
  main main_2 (
    .a(in_2), .b(in_3), .c(in_4), .d(in_5), .a_2(main_2_a_2), .b_2(main_2_b_2), .c_2(main_2_c_2),
    .d_2(main_2_d_2), .e(main_2_e), .f(main_2_f), .g(main_2_g));
  _7_Segment_Display u_7_segment_display_1 (
    .g(main_1_g), .f(main_1_f), .a(main_1_a_2), .b(main_1_b_2), .e(main_1_e), .d(main_1_d_2), .c(main_1_c_2));  // open: dp
  _7_Segment_Display u_7_segment_display_2 (
    .g(main_2_g), .f(main_2_f), .a(main_2_a_2), .b(main_2_b_2), .e(main_2_e), .d(main_2_d_2), .c(main_2_c_2));  // open: dp
endmodule
