// Logisim project shift.circ as structural Verilog: 1 circuit, main circuit main
module main (
  input  [3:0] in_1,
  input  in_2,
  input  in_3,
  input  [1:0] in_4,
  output [3:0] out_5
);

  wire clock_1_out;
  wire [3:0] register_1_q;

  Clock clock_1 (.out(clock_1_out));
  Multiplexer #(.select(2), .enable("false")) multiplexer_1 (
    .in0(register_1_q[2]), .in1(in_3), .in2(register_1_q[3]), .in3(register_1_q[0]), .out(out_5[3]),
    .sel(in_4));
  Register #(.width(4)) register_1 (.D(in_1), .Q(register_1_q), .clk(clock_1_out));  // open: en, clr
  Multiplexer #(.select(2), .enable("false")) multiplexer_2 (
    .in0(register_1_q[1]), .in1(register_1_q[3]), .in2(register_1_q[3]), .in3(register_1_q[3]),
    .out(out_5[2]), .sel(in_4));
  Multiplexer #(.select(2), .enable("false")) multiplexer_3 (
    .in0(register_1_q[0]), .in1(register_1_q[2]), .in2(register_1_q[2]), .in3(register_1_q[2]),
    .out(out_5[1]), .sel(in_4));
  Multiplexer #(.select(2), .enable("false")) multiplexer_4 (
    .in0(in_2), .in1(register_1_q[1]), .in2(register_1_q[1]), .in3(register_1_q[1]), .out(out_5[0]),
    .sel(in_4));
endmodule
